// Logisim project 16BitRegister.circ as structural Verilog: 1 circuit, main circuit main
module main (
  input  [15:0] INPUT,
  input  clk,
  input  Increment,
  input  ld,
  input  clr,
  output [15:0] OUTPUT
);

  wire or_1_out;
  wire [15:0] adder_1_out, multiplexer_1_out;

  Adder #(.width(16)) adder_1 (.a(16'h1), .b(OUTPUT), .out(adder_1_out));  // open: cin, cout
  Multiplexer #(.width(16)) multiplexer_1 (
    .in0(INPUT), .in1(adder_1_out), .out(multiplexer_1_out), .sel(Increment));  // open: en
  Register #(.width(16)) register_1 (.D(multiplexer_1_out), .en(or_1_out), .Q(OUTPUT), .clk(clk), .clr(clr));
  or or_1 (or_1_out, Increment, ld);
endmodule
