// Logisim project DecodeMicropLogic.circ as structural Verilog: 1 circuit, main circuit main
module main (
  input  [2:0] f1,
  input  [2:0] f2,
  input  [2:0] f3,
  output ADD,
  output clr_AC,
  output inc_AC,
  output DRTAC,
  output DRTAR,
  output PCTAR,
  output Write,
  output SUB,
  output OR,
  output AND,
  output Read___mux1,
  output ACTDR___mux2,
  output ACTDR,
  output PCTDR___mux0,
  output XOR,
  output COM,
  output SHL,
  output SHR,
  output inc_PC,
  output ARTPC,
  output Reserved
);

  Decoder #(.select(3)) decoder_1 (
    .out1(ADD), .out2(clr_AC), .out3(inc_AC), .out4(DRTAC), .out5(DRTAR), .out6(PCTAR), .out7(Write), .sel(f1));  // open: out0, en
  Decoder #(.select(3)) decoder_2 (
    .out1(SUB), .out2(OR), .out3(AND), .out4(Read___mux1), .out5(ACTDR___mux2), .out6(ACTDR),
    .out7(PCTDR___mux0), .sel(f2));  // open: out0, en
  Decoder #(.select(3)) decoder_3 (
    .out1(XOR), .out2(COM), .out3(SHL), .out4(SHR), .out5(inc_PC), .out6(ARTPC), .out7(Reserved), .sel(f3));  // open: out0, en
endmodule
