// Logisim project Encode.circ as structural Verilog: 1 circuit, main circuit main
module main (
  input  D0,
  input  D1,
  input  D2,
  output B,
  output A
);

  wire and_1_out, and_2_out, and_3_out, and_4_out, and_6_out, and_7_out, and_8_out, not_1_out, not_2_out,
       not_3_out;

  not not_1 (not_1_out, D0);
  not not_2 (not_2_out, D1);
  not not_3 (not_3_out, D2);
  and and_1 (and_1_out, not_1_out, not_2_out, not_3_out);
  and and_2 (and_2_out, not_1_out, not_2_out, D2);
  and and_3 (and_3_out, not_1_out, D1, not_3_out);
  and and_4 (and_4_out, not_1_out, D1, D2);
  // AND_Gate and_5 has open pins: in0=D0, in1=not_2_out, in2=not_3_out, out=open
  and and_6 (and_6_out, D0, not_2_out, D2);
  and and_7 (and_7_out, D0, D1, not_3_out);
  and and_8 (and_8_out, D0, D1, D2);
  or or_1 (B, and_1_out, and_3_out, and_4_out, and_6_out, and_7_out, and_8_out);
  or or_2 (A, and_1_out, and_2_out, and_4_out, and_6_out, and_7_out, and_8_out);
endmodule
