// Logisim project INCREMENTER.circ as structural Verilog: 1 circuit, main circuit main
module main (
  input  [6:0] INPUT,
  output [6:0] OUTPUT
);

  wire main_1_p4, main_2_p4, main_3_p4, main_4_p4, main_5_p4, main_6_p4;

  // half_Adder_main main_1: pin names not known; wires that end beside it: 1'b1, INPUT[0], OUTPUT[0], main_1_p4
  // half_Adder_main main_2: pin names not known; wires that end beside it: main_1_p4, INPUT[1], OUTPUT[1], main_2_p4
  // half_Adder_main main_3: pin names not known; wires that end beside it: main_2_p4, INPUT[2], OUTPUT[2], main_3_p4
  // half_Adder_main main_4: pin names not known; wires that end beside it: main_3_p4, INPUT[3], OUTPUT[3], main_4_p4
  // half_Adder_main main_5: pin names not known; wires that end beside it: main_4_p4, INPUT[4], OUTPUT[4], main_5_p4
  // half_Adder_main main_6: pin names not known; wires that end beside it: main_5_p4, INPUT[5], OUTPUT[5], main_6_p4
  // half_Adder_main main_7: pin names not known; wires that end beside it: main_6_p4, INPUT[6], OUTPUT[6]
endmodule
