// Logisim project InputLogic.circ as structural Verilog: 1 circuit, main circuit main
module main (
  input  I1,
  input  I0,
  input  T,
  output S1,
  output S0,
  output LD
);

  wire and_2_out, and_5_out, and_6_out, and_7_out, and_8_out, not_1_out, not_2_out, not_3_out;

  not not_1 (not_1_out, I1);
  not not_2 (not_2_out, I0);
  not not_3 (not_3_out, T);
  // AND_Gate and_1 has open pins: in0=not_1_out, in1=not_2_out, in2=not_3_out, out=open
  and and_2 (and_2_out, not_1_out, T, not_2_out);
  // AND_Gate and_3 has open pins: in0=not_1_out, in1=I0, in2=not_3_out, out=open
  and and_4 (LD, not_1_out, I0, T);
  and and_5 (and_5_out, I1, not_2_out, not_3_out);
  and and_6 (and_6_out, I1, T, not_2_out);
  and and_7 (and_7_out, I1, I0, not_3_out);
  and and_8 (and_8_out, I1, I0, T);
  or or_1 (S1, and_5_out, and_6_out, and_7_out, and_8_out);
  or or_2 (S0, and_2_out, LD, and_7_out, and_8_out);
endmodule
