// Logisim project MAIN CIRCUIT.circ as structural Verilog: 1 circuit, main circuit main
module main (
  input  in_1,
  output [10:0] AR,
  output [10:0] PC,
  output [6:0] SBR,
  output [6:0] CAR,
  output [15:0] DR,
  output [15:0] AC,
  output O,
  output U
);

  wire main_2_actdr, main_2_actdr___mux2, main_2_pctdr___mux0, or_1_out, or_2_out, PC_p4, undriven;
  wire [1:0] main_2_drtar, main_2_write, main_3_b, PC_p2;
  wire [2:0] main_1_f1, main_1_f2, main_1_f3;
  wire [10:0] main_2_add, multiplexer_1_out;
  wire [15:0] multiplexer_2_out, ram_1_data;

  Multiplexer #(.width(11)) multiplexer_1 (
    .in0(PC), .in1(DR[10:0]), .out(multiplexer_1_out), .sel(main_2_drtar[0]), .en(undriven));
  or or_1 (or_1_out, main_2_drtar[1], main_2_drtar[0]);
  _11BitRegister_main u_AR (
    .INPUT(multiplexer_1_out), .Increment(1'b0), .ld(or_1_out), .clr(1'b0), .OUTPUT(AR), .clk(PC_p4));
  // _11BitRegister_main PC: pin names not known; wires that end beside it: 1'b0, PC_p2[0], PC_p2[1], PC_p4, AR, PC
  main_main main_1 (
    .AC(AC), .DR(DR), .F1(main_1_f1), .F2(main_1_f2), .F3(main_1_f3), .CLK(PC_p4), .SBR(SBR), .CAR(CAR));
  DecodeMicropLogic_main main_2 (
    .f1(main_1_f1), .f2(main_1_f2), .f3(main_1_f3), .ADD(main_2_add[0]), .clr_AC(main_2_add[1]),
    .inc_AC(main_2_add[2]), .DRTAC(main_2_add[3]), .DRTAR(main_2_drtar[0]), .PCTAR(main_2_drtar[1]),
    .Write(main_2_write[0]), .SUB(main_2_add[4]), .OR(main_2_add[5]), .AND(main_2_add[6]),
    .Read___mux1(main_2_write[1]), .ACTDR___mux2(main_2_actdr___mux2), .ACTDR(main_2_actdr),
    .PCTDR___mux0(main_2_pctdr___mux0), .XOR(main_2_add[7]), .COM(main_2_add[8]), .SHL(main_2_add[9]),
    .SHR(main_2_add[10]), .inc_PC(PC_p2[0]), .ARTPC(PC_p2[1]));  // open: Reserved
  or or_2 (or_2_out, main_2_pctdr___mux0, main_2_write[1], main_2_actdr___mux2);
  Encode_main main_3 (
    .D0(main_2_pctdr___mux0), .D1(main_2_write[1]), .D2(main_2_actdr___mux2), .B(main_3_b[0]), .A(main_3_b[1]));
  Multiplexer #(.select(2), .width(16)) multiplexer_2 (
    .in0({{5{1'b0}}, PC}), .in1(ram_1_data), .in2(AC), .out(multiplexer_2_out), .sel(main_3_b));  // open: in3, en
  _16BitRegister_main u_DR (
    .INPUT(multiplexer_2_out), .Increment(main_2_actdr), .ld(or_2_out), .OUTPUT(DR), .clk(PC_p4));  // open: clr
  Clock clk (.out(PC_p4));
  RAM #(.addrWidth(11), .dataWidth(16), .bus("separate")) ram_1 (
    .addr(AR), .din(DR), .data(ram_1_data), .str(main_2_write[0]), .clk(PC_p4), .ld(main_2_write[1]),
    .clr(in_1));  // open: sel
  ALU_main ALU (.Op(main_2_add), .CLK(PC_p4), .DR(DR), .out(AC), .Overflow(O), .Underflow(U));
endmodule
